// Logisim project Sumador.circ as structural Verilog: 3 circuits, main circuit sumador
module sumador (
  input  A,
  input  B,
  input  Cin,
  output Cout,
  output S
);

  wire and_1_out, and_2_out, and_3_out, or_1_out, xor_1_out;

  and and_1 (and_1_out, A, Cin);
  and and_2 (and_2_out, A, B);
  and and_3 (and_3_out, B, Cin);
  xor xor_1 (xor_1_out, A, B);
  or or_1 (or_1_out, and_1_out, and_2_out);
  or or_2 (Cout, or_1_out, and_3_out);
  xor xor_2 (S, xor_1_out, Cin);
endmodule

module sumador2bits (
  input  A1,
  input  A0,
  input  B1,
  input  B0,
  input  Cin,
  output Cout,
  output S1,
  output S0
);

  wire sumador_1_cout;

  sumador sumador_1 (.A(A0), .B(B0), .Cin(Cin), .Cout(sumador_1_cout), .S(S0));
  sumador sumador_2 (.A(A1), .B(B1), .Cin(sumador_1_cout), .Cout(Cout), .S(S1));
endmodule

module sumador4bits (
  input  A3,
  input  A2,
  input  A1,
  input  A0,
  input  B3,
  input  B2,
  input  B1,
  input  B0,
  input  Cin,
  output S4,
  output S3,
  output S2,
  output S1,
  output S0
);

  wire sumador2bits_1_cout;

  sumador2bits sumador2bits_1 (
    .A1(A1), .A0(A0), .B1(B1), .B0(B0), .Cin(Cin), .Cout(sumador2bits_1_cout), .S1(S1), .S0(S0));
  sumador2bits sumador2bits_2 (
    .A1(A3), .A0(A2), .B1(B3), .B0(B2), .Cin(sumador2bits_1_cout), .Cout(S4), .S1(S3), .S0(S2));
endmodule
