// Logisim project actividad19mayo.circ as structural Verilog: 3 circuits, main circuit a326
module a326 (
  input  A,
  input  B,
  input  C,
  output X
);

  wire and_1_out, and_2_out, not_1_out, not_2_out;

  not not_1 (not_1_out, A);
  not not_2 (not_2_out, C);
  and and_1 (and_1_out, not_1_out, B);
  and and_2 (and_2_out, and_1_out, not_2_out);
  not not_3 (X, and_2_out);
endmodule

module b326 (
  input  A,
  input  B,
  input  C,
  output X
);

  wire and_1_out, not_1_out, not_2_out, or_1_out;

  not not_1 (not_1_out, A);
  not not_2 (not_2_out, B);
  and and_1 (and_1_out, not_2_out, C);
  or or_1 (or_1_out, not_1_out, and_1_out);
  not not_3 (X, or_1_out);
endmodule

module c326 (
  input  A,
  input  B,
  input  C,
  input  D,
  output X
);

  wire and_1_out, and_2_out, and_3_out, not_1_out;

  and and_1 (and_1_out, A, B);
  and and_2 (and_2_out, C, D);
  not not_1 (not_1_out, and_2_out);
  and and_3 (and_3_out, and_1_out, not_1_out);
  not not_2 (X, and_3_out);
endmodule
